# Fritzing sketch ayak ısıtıcı şeması (saved by Fritzing 0.9.3b)
breadboards: 1

parts:
  R1 = Resistor [tolerance=±5% resistance=10k package=THT]
  R2 = Resistor [tolerance=±5% resistance=10k package=THT]
  R3 = Rotary Potentiometer (Small) [maximum_resistance=100kΩ package=THT]
  Power_plug1 = Power plug
  Q1 = Basic FET N-Channel [package="TO220 [THT]"]
  U1 = Voltage Regulator - 5V [package="TO220 [THT]"]
  R4 = Temperature Sensor (Thermistor) [thermistor_type=NTC package=THT]
  Parça1 = Arduino Uno (Rev3)

nets:
  N1: R1.Pin_0, R4.pin_1, Parça1.A5/SCL
  GND: R1.Pin_1, R2.Pin_1, R3.leg1, Power_plug1.GND, Q1.source, U1.GND, Parça1.GND
  N2: R2.Pin_0, Q1.gate, Parça1.D13/SCK
  N3: R3.wiper, Parça1.A4/SDA
  N4: R3.leg2, U1.output_voltage, R4.pin_0, Parça1.5V
  N5: Power_plug1.VCC, U1.input_voltage

notes:
  pin bilgileri:
  G, D, S
  ısıtıcı '+' çıkış
  ısıtıcı '-' çıkış
  <==
  12V giriş
  NTC sensör ==>
  (Voltaj regülatör
  arduino pro mini ile yapmak isteyenler için)
